# Fritzing sketch layout (saved by Fritzing 0.9.3b)
perfboards: 1

parts:
  Componente1 = Arduino Nano (Rev3.0)
  Q1 = TRANSISTOR_NPN [package=to-92]
  R1 = Resistor [tolerance=±5% resistance=220 package="0402 [SMD]"]
  S1 = SWITCH-MOMENTARY-2 [package=tactile-pth]  # not connected
  S2 = SWITCH-MOMENTARY-2 [package=tactile-pth]  # not connected
  S3 = SWITCH-MOMENTARY-2 [package=tactile-pth]  # not connected
  VCC1 = Battery block 9V
  U1 = POT_SWITCH [package=pot_pth]  # not connected

nets:
  N1: Componente1.D2, R1.Pin_0
  N2: Componente1.VIN, VCC1.+
  N3: Q1.C, R1.Pin_1
